// Logisim project ICs.circ as structural Verilog: 4 circuits, main circuit IC 7408 (2-input AND)
module IC_7408__2_input_AND (
  input  in_1,
  input  in_2,
  input  in_3,
  input  in_4,
  input  in_5,
  input  in_6,
  input  in_7,
  input  in_8,
  output out_9,
  output out_10,
  output out_11,
  output out_12
);

  and and_1 (out_9, in_1, in_3);
  and and_2 (out_11, in_5, in_7);
  and and_3 (out_10, in_2, in_4);
  and and_4 (out_12, in_6, in_8);
endmodule

module IC_7432__2_input_OR (
  input  in_1,
  input  in_2,
  input  in_3,
  input  in_4,
  input  in_5,
  input  in_6,
  input  in_7,
  input  in_8,
  output out_9,
  output out_10,
  output out_11,
  output out_12
);

  or or_1 (out_9, in_1, in_3);
  or or_2 (out_11, in_5, in_7);
  or or_3 (out_10, in_2, in_4);
  or or_4 (out_12, in_6, in_8);
endmodule

module IC_7486__2_input_XOR (
  input  in_1,
  input  in_2,
  input  in_3,
  input  in_4,
  input  in_5,
  input  in_6,
  input  in_7,
  input  in_8,
  output out_9,
  output out_10,
  output out_11,
  output out_12
);

  xor xor_1 (out_9, in_1, in_3);
  xor xor_2 (out_11, in_5, in_7);
  xor xor_3 (out_10, in_2, in_4);
  xor xor_4 (out_12, in_6, in_8);
endmodule

module IC_7404__Inverters (
  input  in_1,
  input  in_2,
  input  in_3,
  input  in_4,
  input  in_5,
  input  in_6,
  output out_7,
  output out_8,
  output out_9,
  output out_10,
  output out_11,
  output out_12
);

  not not_1 (out_7, in_1);
  not not_2 (out_9, in_3);
  not not_3 (out_11, in_5);
  not not_4 (out_8, in_2);
  not not_5 (out_10, in_4);
  not not_6 (out_12, in_6);
endmodule
